# Fritzing sketch IMU_Steering_Bot (saved by Fritzing 0.7.0b)
breadboards: 1

parts:
  Arduino1 = Arduino
  J1 = Basic Servo
  J2 = Basic Servo
  U1 = MinIMU-9

nets:
  N1: Arduino1.D10, J2.pulse
  N2: Arduino1.D9, J1.pulse
  VCC: Arduino1.+5V, J1.vcc, J2.vcc, U1.VIN
  GND: Arduino1.GND, J1.gnd, J2.gnd, U1.GND
  N3: Arduino1.A4, U1.SDA
  N4: Arduino1.A5, U1.SCL

notes:
  This file is included with IMU_Steering_Bot.
  See (https://github.com/dougbot/IMU_Steering_Bot)

custom parts:
  MinIMU-9: MinIMU-9 9-axis compass/accelerometer/gyro. I2C interface.
